# Fritzing sketch Buzzer-Microphone (saved by Fritzing 0.8.7b)
breadboards: 1

parts:
  Part1 = Breakout Board for Electret Microphone
  R2 = Resistor [tolerance=±5% resistance=2.2k package=THT]
  Piezo1 = Piezo Speaker - PC Mount [part_number=COM-07950]
  Part2 = Intel Edison

nets:
  N1: Part1.VCC, Part2.A0
  N2: Part1.GND, R2.Pin_0
  N3: Part1.AUD, Part2.3V3
  N4: R2.Pin_1, Piezo1.VCC
  N5: Piezo1.GND, Part2.D3_PWM

custom parts:
  Piezo Speaker - PC Mount: This is a small 12mm round speaker that operates around the audible 2kHz range. You can use these speakers to create simple music or user interfaces. Each speaker is PTH solderable and requires an operating voltage of 3.5-5V with a mean current of 35mA max. These speakers also have a typical sound output of 95 dBA and a coil resistance of 42 ±6.3 ohms.
  Intel Edison: The Intel® Edison development platform is designed to lower the barriers to entry for a range of inventors, entrepreneurs, and consumer product designers to rapidly prototype and produce “Internet of Things” (IoT) and wearable computing products.
